# Fritzing sketch radio_game (saved by Fritzing 0.9.4)
breadboards: 1

parts:
  Part1 = Arduino Uno (Rev3)
  Part2 = NRF24L01+ Breakout Board
  S1 = Pushbutton [package="[SMD]"]
  LED1 = smd LED [color="Green (555nm)" package="0805 [SMD]"]
  LED2 = smd LED [color="Red (633nm)" package="0805 [SMD]"]
  R1 = Resistor [tolerance=±5% resistance=220 package="0402 [SMD]"]
  R2 = Resistor [tolerance=±5% resistance=220 package="0402 [SMD]"]

nets:
  N1: Part1.D8, Part2.CS
  N2: Part1.D11_PWM/MOSI, Part2.MOSI
  N3: Part1.D12/MISO, Part2.MISO
  N4: Part1.D13/SCK, Part2.SCK
  GND: Part1.GND, Part2.GND, S1.Pin_3, S1.Pin_4, R1.Pin_0, R2.Pin_0
  N5: Part1.D4, S1.Pin_1, S1.Pin_2
  N6: Part1.D5_PWM, LED2.anode
  N7: Part1.D6_PWM, LED1.anode
  N8: Part1.D7, Part2.CE
  3V3: Part1.3V3, Part2.VCC
  N9: LED1.cathode, R1.Pin_1
  N10: LED2.cathode, R2.Pin_1
