# Fritzing sketch iot_thermometer (saved by Fritzing 0.9.4)
breadboards: 1

parts:
  U1 = NodeMCU V1.0
  DHT1 = DHT22 Humidity and Temperature Sensor
  R1 = Resistor [tolerance=±5% resistance=10k package="2512 [SMD]"]

nets:
  N1: U1.D2, DHT1.DATA, R1.Pin_0
  3V3: U1.3V3, DHT1.VDD, R1.Pin_1
  GND: U1.GND, DHT1.GND

custom parts:
  NodeMCU V1.0: ESP8266 based NodeMCU
