# Fritzing sketch rgb_controller (saved by Fritzing 0.9.4)
breadboards: 1

parts:
  U1 = NodeMCU V1.0
  LED1 = RGB LED (com. cathode, rbg) [package="5 mm [THT]"]
  R1 = Resistor [tolerance=±5% resistance=220 package=THT]
  R2 = Resistor [tolerance=±5% resistance=220 package=THT]
  R3 = Resistor [tolerance=±5% resistance=220 package=THT]

nets:
  N1: U1.D1, R1.Pin_1
  N2: U1.D2, R2.Pin_1
  N3: U1.D4, R3.Pin_1
  N4: U1.GND, LED1.common_cathode
  N5: LED1.red_anode, R1.Pin_0
  N6: LED1.blue_anode, R2.Pin_0
  N7: LED1.green_anode, R3.Pin_0

custom parts:
  NodeMCU V1.0: ESP8266 based NodeMCU
