# Fritzing sketch russian_roulette (saved by Fritzing 0.9.4)
breadboards: 1

parts:
  Part1 = Arduino Uno (Rev3)
  J1 = Piezo Speaker
  LED1 = LED - 5mm [color="Blue (470nm)" package="5 mm [THT]"]
  R1 = Resistor [tolerance=±5% resistance=220 package=THT]
  S1 = Pushbutton [package="[THT]"]
  LED2 = LED - 5mm [color="Red (633nm)" package="5 mm [THT]"]
  LED3 = LED - 5mm [color="Red (633nm)" package="5 mm [THT]"]
  LED4 = LED - 5mm [color="Red (633nm)" package="5 mm [THT]"]
  LED5 = LED - 5mm [color="Red (633nm)" package="5 mm [THT]"]
  LED6 = LED - 5mm [color="Red (633nm)" package="5 mm [THT]"]

nets:
  N1: Part1.D8, J1.pin2
  N2: Part1.GND, J1.pin1, R1.Pin_0, S1.Pin_3, S1.Pin_4
  N3: Part1.D2, LED1.anode
  N4: Part1.D3_PWM, LED4.anode
  N5: Part1.D4, LED3.anode
  N6: Part1.D5_PWM, LED2.anode
  N7: Part1.D6_PWM, LED5.anode
  N8: Part1.D7, LED6.anode
  N9: LED1.cathode, R1.Pin_1, LED2.cathode, LED4.cathode, LED5.cathode, LED6.cathode
  N10: S1.Pin_1, S1.Pin_2
