# Fritzing sketch wifi_game (saved by Fritzing 0.9.4)
breadboards: 1

parts:
  U1 = NodeMCU V1.0
  R1 = Resistor [tolerance=±5% resistance=220 package=THT]
  R2 = Resistor [tolerance=±5% resistance=220 package=THT]
  S1 = Pushbutton [package="[THT]"]
  LED1 = LED - 5mm [color="Red (633nm)" package="5 mm [THT]"]
  LED2 = LED - 5mm [color="Green (555nm)" package="5 mm [THT]"]

nets:
  N1: U1.D1, LED1.anode
  N2: U1.D2, LED2.anode
  N3: U1.GND, R1.Pin_0, R2.Pin_0, S1.Pin_1, S1.Pin_2
  N4: U1.D5, S1.Pin_3, S1.Pin_4
  N5: R1.Pin_1, LED1.cathode
  N6: R2.Pin_1, LED2.cathode

custom parts:
  NodeMCU V1.0: ESP8266 based NodeMCU
